// Logisim project modelo_banco_registradores.circ as structural Verilog: 6 circuits, main circuit Bloco_Registradores
module Bloco_Registradores (
  input  [15:0] Data_in,
  input  Load,
  input  [15:0] Address_A_OUT,
  input  [1:0] Address_A,
  input  [1:0] Data_address,
  input  [15:0] Address_B_OUT,
  input  [1:0] Address_B,
  input  Clock
);

  wire and_1_out, and_2_out, and_3_out, decoder_1_out0, decoder_1_out1, decoder_1_out2;
  wire [15:0] R1_q, R2_q, R3_q;

  Decoder #(.select(2)) decoder_1 (
    .out0(decoder_1_out0), .out1(decoder_1_out1), .out2(decoder_1_out2), .sel(Data_address));  // open: out3, en
  Register #(.width(16)) R1 (.D(Data_in), .en(and_1_out), .clk(Clock), .Q(R1_q), .clr(1'b0));
  and and_1 (and_1_out, Load, decoder_1_out0);
  Register #(.width(16)) R2 (.D(Data_in), .en(and_2_out), .clk(Clock), .Q(R2_q), .clr(1'b0));
  and and_2 (and_2_out, Load, decoder_1_out1);
  Register #(.width(16)) R3 (.D(Data_in), .en(and_3_out), .clk(Clock), .Q(R3_q), .clr(1'b0));
  and and_3 (and_3_out, Load, decoder_1_out2);
  Multiplexer #(.select(2), .width(16)) multiplexer_1 (
    .in0({16{1'b0}}), .in1(R1_q), .in2(R2_q), .in3(R3_q), .out(Address_A_OUT), .sel(Address_A));
  Multiplexer #(.select(2), .width(16)) multiplexer_2 (
    .in0({16{1'b0}}), .in1(R1_q), .in2(R2_q), .in3(R3_q), .out(Address_B_OUT), .sel(Address_B));

  // Notes on the sheet:
  //   Data_in: initial=0x1
  //   R0
endmodule

module ULA (
  input  [15:0] Operando_A,
  input  [15:0] Resultado_ULA,
  input  [15:0] Operando_B
);

  Adder #(.width(16)) adder_1 (.a(Operando_A), .b(Operando_B), .out(Resultado_ULA));  // open: cin, cout
endmodule

module CPU_Principal (
  input  Mem_to_Reg
);

  wire [15:0] multiplexer_1_out, undriven, undriven_2, undriven_3;

  Multiplexer #(.width(16)) multiplexer_1 (.in0(undriven), .out(multiplexer_1_out), .sel(Mem_to_Reg));  // open: in1
  clock_marcelo clock_marcelo_1 ();
  Bloco_Registradores bloco_registradores_1 (
    .Data_in(multiplexer_1_out), .Address_A_OUT(undriven_2), .Address_B_OUT(undriven_3));  // open: Load, Address_A, Data_address, Address_B, Clock
  ULA ula_1 (.Operando_A(undriven_2), .Resultado_ULA(undriven), .Operando_B(undriven_3));
endmodule

module Unidade_de_Controle (
  input  [1:0] Opcode,
  output Mem_to_Reg,
  output MemWrite,
  output Load
);

  wire decoder_1_out2;

  Decoder #(.select(2)) decoder_1 (
    .out0(Mem_to_Reg), .out1(MemWrite), .out2(decoder_1_out2), .sel(Opcode), .en(1'b1));  // open: out3
  or or_1 (Load, Mem_to_Reg, decoder_1_out2);
endmodule

module Memorias_IR_Murilo (
  input  [4:0] PC_Address,
  input  Clock,
  input  Reset,
  input  [4:0] Data_Address,
  input  MemWrite,
  input  [15:0] Data_Write,
  output [1:0] Opcode,
  output [1:0] RD_RS2,
  output [1:0] RS1,
  output [1:0] RS2,
  output [7:0] Immediate,
  output [15:0] Instruction_IR,
  output [15:0] Data_Read
);

  wire [15:0] Instruction_Memory_data;

  ROM #(.addrWidth(5), .dataWidth(16)) Instruction_Memory (.addr(PC_Address), .data(Instruction_Memory_data));
  RAM #(.addrWidth(5), .asyncread("true"), .dataWidth(16), .databus("bibus"), .\type ("nonvolatile")) Data_Memory (
    .addr(Data_Address), .we(MemWrite), .oe(1'b1), .clk(Clock), .din(Data_Write), .dout(Data_Read));
  Register #(.width(16)) IR (
    .D(Instruction_Memory_data), .en(1'b1), .clk(Clock), .Q({Instruction_IR[15:8], Immediate}), .clr(Reset));

  assign Instruction_IR[7:0] = Immediate;
  assign Opcode = Instruction_IR[15:14];
  assign RD_RS2 = Instruction_IR[13:12];
  assign RS1 = Instruction_IR[11:10];
  assign RS2 = Instruction_IR[9:8];

  // Notes on the sheet:
  //   MEMORIA DE INSTRUCOES 32 x 16
  //   contents of Instruction_Memory (hex, n*v repeats v):
  //   100a 200b b600 700c
  //   ROM: 100A 200B B600 700C
  //   MEMORIA DE DADOS 32 x 16
  //   Teste: inicializar Mem[10] = 7 e Mem[11] = 5
  //   IR E DECODIFICACAO DOS CAMPOS
endmodule

module clock_marcelo (
);

  wire clk_out, reset_out;
  wire [4:0] adder_1_out, PC_q;
  wire [15:0] IR_q, undriven;

  Clock clk (.out(clk_out));
  Button reset (.out(reset_out));
  Register #(.width(5)) PC (.D(adder_1_out), .clk(clk_out), .Q(PC_q), .clr(reset_out));  // open: en
  Adder #(.width(5)) adder_1 (.a(PC_q), .b(5'b00001), .out(adder_1_out));  // open: cin, cout
  RAM #(.addrWidth(5), .asyncread("true"), .dataWidth(16), .databus("bidir")) Instruction_Memory (
    .addr(PC_q), .we(1'b0), .oe(1'b1));  // open: clk, data
  Register #(.width(16)) IR (.D(undriven), .Q(IR_q), .clk(clk_out));  // open: en, clr
  // Probe on IR_q[15:14]
  // Probe on IR_q[13:12]
  // Probe on IR_q[11:10]
  // Probe on IR_q[9:8]
  // Probe on IR_q[7:0]
endmodule
